# Fritzing sketch main_circuit_diagram (saved by Fritzing 0.9.6b)
circuit board: 8.46667cm x 5.64444cm
breadboards: 1

parts:
  Part1 = InvenSense MPU6050
  WeMos_D1_Mini1 = WeMos D1 Mini
  U2 = LIPO-110mAh [package=lipo-110]

nets:
  VCC: Part1.VCC, WeMos_D1_Mini1.3V3
  N1: Part1.GND, WeMos_D1_Mini1.G, U2.-
  N2: Part1.SCL, WeMos_D1_Mini1.D1
  N3: Part1.SDA, WeMos_D1_Mini1.D2
  N4: WeMos_D1_Mini1.5V, U2.+
